# Fritzing sketch schema (saved by Fritzing 0.9.3b)

parts:
  WeMos_D1_Mini1 = WeMos D1 Mini
  WeMos_D1_Mini_OLED_Shield1 = WeMos D1 Mini OLED Shield  # not connected
  M1 = DC Motor
  VCC1 = 4 x AAA Battery Mount
  S1 = H-Bridge with L298N
  M2 = DC Motor

nets:
  5V: WeMos_D1_Mini1.5V, S1.5V
  N1: WeMos_D1_Mini1.D5, S1.IN4
  N2: WeMos_D1_Mini1.D6, S1.IN3
  N3: WeMos_D1_Mini1.D7, S1.IN1
  N4: WeMos_D1_Mini1.D8, S1.IN2
  N5: WeMos_D1_Mini1.G, VCC1.-, S1.GND
  N6: M1.pin_1, S1.M1-02
  N7: M1.pin_2, S1.M1-01
  N8: VCC1.+, S1.12V
  N9: S1.ENA, S1.ENA-5V
  N10: S1.ENB, S1.ENB-5V
  N11: S1.M2-01, M2.pin_1
  N12: S1.M2-02, M2.pin_2

custom parts:
  H-Bridge with L298N: h-bridge
